// Logisim project cpu_design_logisim.circ as structural Verilog: 12 circuits, main circuit main
module main (
  input  Clk,
  input  Rst
);

  wire and_1_out, clock_1_out, controlled_buffer_40_out, not_1_out, not_2_out, program_control_unit_1_alu_in,
       program_control_unit_1_alu_out, program_control_unit_1_alu_write_a,
       program_control_unit_1_alu_write_b, program_control_unit_1_alu_write_f,
       program_control_unit_1_alu_write_out, program_control_unit_1_connect_f_to_data_bus,
       program_control_unit_1_eau_address_bus_in, program_control_unit_1_eau_data_bus_in,
       program_control_unit_1_eau_hi_select, program_control_unit_1_eau_low_select,
       program_control_unit_1_jump_enable, program_control_unit_1_lsu_decrement_stack_pointer,
       program_control_unit_1_lsu_flags_out, program_control_unit_1_lsu_increment_stack_pointer,
       program_control_unit_1_lsu_ram_enable, program_control_unit_1_lsu_read_enable,
       program_control_unit_1_lsu_rom_enable, program_control_unit_1_lsu_write_enable,
       program_control_unit_1_pc_address_bus_in, program_control_unit_1_pc_address_bus_out,
       program_control_unit_1_pc_enable_unused, program_control_unit_1_pc_load_value,
       program_control_unit_1_pc_skip_to_next_instruction, program_control_unit_1_rf_a_in,
       program_control_unit_1_rf_a_out, program_control_unit_1_rf_b_in, program_control_unit_1_rf_b_out,
       program_control_unit_1_rf_c_in, program_control_unit_1_rf_c_out, program_control_unit_1_rf_d_in,
       program_control_unit_1_rf_d_out, program_control_unit_1_rf_flags_in,
       program_control_unit_1_rf_flags_out, program_control_unit_1_rf_temp_in,
       program_control_unit_1_rf_temp_out, program_control_unit_1_stack_node_enable, pull_resistor_2_node,
       pull_resistor_3_node, pull_resistor_4_node, pull_resistor_5_node, pull_resistor_6_node,
       pull_resistor_7_node, pull_resistor_8_node, pull_resistor_9_node, pull_resistor_10_node,
       pull_resistor_11_node, pull_resistor_12_node, pull_resistor_13_node, pull_resistor_14_node,
       pull_resistor_15_node, pull_resistor_16_node, pull_resistor_17_node, pull_resistor_18_node,
       pull_resistor_20_node, pull_resistor_21_node, pull_resistor_22_node, pull_resistor_23_node,
       pull_resistor_24_node, pull_resistor_25_node, pull_resistor_26_node, pull_resistor_27_node,
       pull_resistor_28_node, pull_resistor_29_node, pull_resistor_30_node, pull_resistor_31_node,
       pull_resistor_32_node, pull_resistor_33_node, pull_resistor_34_node, pull_resistor_35_node, xor_1_out;
  wire [2:0] program_counter_driver_1_iso;
  wire [6:0] program_control_unit_1_alu_op, pull_resistor_19_node;
  wire [7:0] alu_driver_1_fo, program_control_unit_1_dbo, program_control_unit_1_iro, pull_resistor_37_node,
       register_file_1_fod;
  wire [15:0] program_counter_driver_1_abo;

  Clock clock_1 (.out(clock_1_out));
  not not_1 (not_1_out, register_file_1_fod[3]);
  buf and_1 (and_1_out, clock_1_out);  // AND_Gate
  Pull_Resistor pull_resistor_1 (.node(and_1_out));
  xor xor_1 (xor_1_out, and_1_out, Clk);
  Pull_Resistor pull_resistor_2 (.node(pull_resistor_2_node));
  Pull_Resistor pull_resistor_3 (.node(pull_resistor_3_node));
  not not_2 (not_2_out, Rst);
  assign pull_resistor_3_node = not_2_out ? program_control_unit_1_rf_a_in : 1'bz;  // Controlled_Buffer controlled_buffer_1
  assign pull_resistor_2_node = not_2_out ? program_control_unit_1_rf_b_in : 1'bz;  // Controlled_Buffer controlled_buffer_2
  program_control_unit program_control_unit_1 (
    .Rst(Rst), .Clk(xor_1_out), .Isi(program_counter_driver_1_iso), .Dbi(program_control_unit_1_dbo),
    .Fi(register_file_1_fod), .RF_A_IN(program_control_unit_1_rf_a_in),
    .RF_B_IN(program_control_unit_1_rf_b_in), .RF_C_IN(program_control_unit_1_rf_c_in),
    .RF_D_IN(program_control_unit_1_rf_d_in), .RF_FLAGS_IN(program_control_unit_1_rf_flags_in),
    .RF_A_OUT(program_control_unit_1_rf_a_out), .RF_B_OUT(program_control_unit_1_rf_b_out),
    .RF_C_OUT(program_control_unit_1_rf_c_out), .RF_D_OUT(program_control_unit_1_rf_d_out),
    .RF_FLAGS_OUT(program_control_unit_1_rf_flags_out), .ALU_IN(program_control_unit_1_alu_in),
    .ALU_OUT(program_control_unit_1_alu_out), .ALU_WRITE_OUT(program_control_unit_1_alu_write_out),
    .ALU_WRITE_F(program_control_unit_1_alu_write_f), .ALU_WRITE_B(program_control_unit_1_alu_write_b),
    .ALU_WRITE_A(program_control_unit_1_alu_write_a), .ALU_OP(program_control_unit_1_alu_op),
    .LSU_INCREMENT_STACK_POINTER(program_control_unit_1_lsu_increment_stack_pointer),
    .LSU_DECREMENT_STACK_POINTER(program_control_unit_1_lsu_decrement_stack_pointer),
    .LSU_ROM_ENABLE(program_control_unit_1_lsu_rom_enable),
    .LSU_RAM_ENABLE(program_control_unit_1_lsu_ram_enable),
    .LSU_READ_ENABLE(program_control_unit_1_lsu_read_enable),
    .LSU_WRITE_ENABLE(program_control_unit_1_lsu_write_enable),
    .LSU_FLAGS_OUT(program_control_unit_1_lsu_flags_out),
    .EAU_HI_SELECT(program_control_unit_1_eau_hi_select),
    .EAU_LOW_SELECT(program_control_unit_1_eau_low_select),
    .EAU_DATA_BUS_IN(program_control_unit_1_eau_data_bus_in),
    .EAU_ADDRESS_BUS_IN(program_control_unit_1_eau_address_bus_in),
    .PC_ADDRESS_BUS_IN(program_control_unit_1_pc_address_bus_in),
    .PC_ADDRESS_BUS_OUT(program_control_unit_1_pc_address_bus_out),
    .PC_SKIP_TO_NEXT_INSTRUCTION(program_control_unit_1_pc_skip_to_next_instruction),
    .PC_ENABLE_UNUSED(program_control_unit_1_pc_enable_unused),
    .PC_LOAD_VALUE(program_control_unit_1_pc_load_value),
    .CONNECT_F_TO_DATA_BUS(program_control_unit_1_connect_f_to_data_bus),
    .RF_TEMP_IN(program_control_unit_1_rf_temp_in), .RF_TEMP_OUT(program_control_unit_1_rf_temp_out),
    .JUMP_ENABLE(program_control_unit_1_jump_enable), .Dbo(program_control_unit_1_dbo),
    .Iro(program_control_unit_1_iro), .STACK_NODE_ENABLE(program_control_unit_1_stack_node_enable));
  Pull_Resistor pull_resistor_4 (.node(pull_resistor_4_node));
  Pull_Resistor pull_resistor_5 (.node(pull_resistor_5_node));
  Pull_Resistor pull_resistor_6 (.node(pull_resistor_6_node));
  Pull_Resistor pull_resistor_7 (.node(pull_resistor_7_node));
  assign pull_resistor_7_node = not_2_out ? program_control_unit_1_rf_c_in : 1'bz;  // Controlled_Buffer controlled_buffer_3
  assign pull_resistor_6_node = not_2_out ? program_control_unit_1_rf_d_in : 1'bz;  // Controlled_Buffer controlled_buffer_4
  assign pull_resistor_5_node = not_2_out ? program_control_unit_1_rf_flags_in : 1'bz;  // Controlled_Buffer controlled_buffer_5
  assign pull_resistor_4_node = not_2_out ? program_control_unit_1_rf_a_out : 1'bz;  // Controlled_Buffer controlled_buffer_6
  Pull_Resistor pull_resistor_8 (.node(pull_resistor_8_node));
  Pull_Resistor pull_resistor_9 (.node(pull_resistor_9_node));
  Pull_Resistor pull_resistor_10 (.node(pull_resistor_10_node));
  Pull_Resistor pull_resistor_11 (.node(pull_resistor_11_node));
  assign pull_resistor_11_node = not_2_out ? program_control_unit_1_rf_b_out : 1'bz;  // Controlled_Buffer controlled_buffer_7
  assign pull_resistor_10_node = not_2_out ? program_control_unit_1_rf_c_out : 1'bz;  // Controlled_Buffer controlled_buffer_8
  assign pull_resistor_9_node = not_2_out ? program_control_unit_1_rf_d_out : 1'bz;  // Controlled_Buffer controlled_buffer_9
  assign pull_resistor_8_node = not_2_out ? program_control_unit_1_rf_flags_out : 1'bz;  // Controlled_Buffer controlled_buffer_10
  Pull_Resistor pull_resistor_12 (.node(pull_resistor_12_node));
  Pull_Resistor pull_resistor_13 (.node(pull_resistor_13_node));
  Pull_Resistor pull_resistor_14 (.node(pull_resistor_14_node));
  Pull_Resistor pull_resistor_15 (.node(pull_resistor_15_node));
  assign pull_resistor_15_node = not_2_out ? program_control_unit_1_alu_in : 1'bz;  // Controlled_Buffer controlled_buffer_11
  assign pull_resistor_14_node = not_2_out ? program_control_unit_1_alu_out : 1'bz;  // Controlled_Buffer controlled_buffer_12
  assign pull_resistor_13_node = not_2_out ? program_control_unit_1_alu_write_out : 1'bz;  // Controlled_Buffer controlled_buffer_13
  assign pull_resistor_12_node = not_2_out ? program_control_unit_1_alu_write_f : 1'bz;  // Controlled_Buffer controlled_buffer_14
  Pull_Resistor pull_resistor_16 (.node(pull_resistor_16_node));
  Pull_Resistor pull_resistor_17 (.node(pull_resistor_17_node));
  Pull_Resistor pull_resistor_18 (.node(pull_resistor_18_node));
  Pull_Resistor pull_resistor_19 (.node(pull_resistor_19_node));
  assign pull_resistor_17_node = not_2_out ? program_control_unit_1_alu_write_b : 1'bz;  // Controlled_Buffer controlled_buffer_15
  assign pull_resistor_16_node = not_2_out ? program_control_unit_1_alu_write_a : 1'bz;  // Controlled_Buffer controlled_buffer_16
  assign pull_resistor_19_node = not_2_out ? program_control_unit_1_alu_op : 7'bz;  // Controlled_Buffer controlled_buffer_17
  assign pull_resistor_18_node = not_2_out ? program_control_unit_1_lsu_increment_stack_pointer : 1'bz;  // Controlled_Buffer controlled_buffer_18
  Pull_Resistor pull_resistor_20 (.node(pull_resistor_20_node));
  Pull_Resistor pull_resistor_21 (.node(pull_resistor_21_node));
  Pull_Resistor pull_resistor_22 (.node(pull_resistor_22_node));
  Pull_Resistor pull_resistor_23 (.node(pull_resistor_23_node));
  assign pull_resistor_23_node = not_2_out ? program_control_unit_1_lsu_decrement_stack_pointer : 1'bz;  // Controlled_Buffer controlled_buffer_19
  assign pull_resistor_22_node = not_2_out ? program_control_unit_1_lsu_rom_enable : 1'bz;  // Controlled_Buffer controlled_buffer_20
  assign pull_resistor_21_node = not_2_out ? program_control_unit_1_lsu_ram_enable : 1'bz;  // Controlled_Buffer controlled_buffer_21
  assign pull_resistor_20_node = not_2_out ? program_control_unit_1_lsu_read_enable : 1'bz;  // Controlled_Buffer controlled_buffer_22
  Pull_Resistor pull_resistor_24 (.node(pull_resistor_24_node));
  Pull_Resistor pull_resistor_25 (.node(pull_resistor_25_node));
  Pull_Resistor pull_resistor_26 (.node(pull_resistor_26_node));
  Pull_Resistor pull_resistor_27 (.node(pull_resistor_27_node));
  assign pull_resistor_27_node = not_2_out ? program_control_unit_1_lsu_write_enable : 1'bz;  // Controlled_Buffer controlled_buffer_23
  assign pull_resistor_26_node = not_2_out ? program_control_unit_1_lsu_flags_out : 1'bz;  // Controlled_Buffer controlled_buffer_24
  assign pull_resistor_25_node = not_2_out ? program_control_unit_1_eau_hi_select : 1'bz;  // Controlled_Buffer controlled_buffer_25
  assign pull_resistor_24_node = not_2_out ? program_control_unit_1_eau_low_select : 1'bz;  // Controlled_Buffer controlled_buffer_26
  Pull_Resistor pull_resistor_28 (.node(pull_resistor_28_node));
  Pull_Resistor pull_resistor_29 (.node(pull_resistor_29_node));
  Pull_Resistor pull_resistor_30 (.node(pull_resistor_30_node));
  Pull_Resistor pull_resistor_31 (.node(pull_resistor_31_node));
  assign pull_resistor_29_node = not_2_out ? program_control_unit_1_pc_address_bus_in : 1'bz;  // Controlled_Buffer controlled_buffer_27
  assign pull_resistor_28_node = not_2_out ? program_control_unit_1_pc_address_bus_out : 1'bz;  // Controlled_Buffer controlled_buffer_28
  assign pull_resistor_31_node = not_2_out ? program_control_unit_1_eau_data_bus_in : 1'bz;  // Controlled_Buffer controlled_buffer_29
  assign pull_resistor_30_node = not_2_out ? program_control_unit_1_eau_address_bus_in : 1'bz;  // Controlled_Buffer controlled_buffer_30
  Pull_Resistor pull_resistor_32 (.node(pull_resistor_32_node));
  Pull_Resistor pull_resistor_33 (.node(pull_resistor_33_node));
  assign program_control_unit_1_dbo = pull_resistor_34_node ? alu_driver_1_fo : 8'bz;  // Controlled_Buffer controlled_buffer_31
  Pull_Resistor pull_resistor_34 (.node(pull_resistor_34_node));
  Pull_Resistor pull_resistor_35 (.node(pull_resistor_35_node));
  assign pull_resistor_33_node = not_2_out ? program_control_unit_1_pc_skip_to_next_instruction : 1'bz;  // Controlled_Buffer controlled_buffer_32
  assign pull_resistor_32_node = not_2_out ? program_control_unit_1_pc_enable_unused : 1'bz;  // Controlled_Buffer controlled_buffer_33
  assign pull_resistor_35_node = not_2_out ? program_control_unit_1_pc_load_value : 1'bz;  // Controlled_Buffer controlled_buffer_34
  assign pull_resistor_34_node = not_2_out ? program_control_unit_1_connect_f_to_data_bus : 1'bz;  // Controlled_Buffer controlled_buffer_35
  // Probe on program_control_unit_1_dbo
  // Probe on program_counter_driver_1_abo
  // Probe on alu_driver_1_fo
  // Probe on pull_resistor_19_node
  Pull_Resistor pull_resistor_36 (.node(program_control_unit_1_dbo));
  Controlled_Buffer controlled_buffer_36 (.in(program_control_unit_1_rf_temp_in), .en(not_2_out));  // open: out
  Controlled_Buffer controlled_buffer_37 (.in(program_control_unit_1_rf_temp_out), .en(not_2_out));  // open: out
  Controlled_Buffer controlled_buffer_38 (.in(program_control_unit_1_jump_enable), .en(not_2_out));  // open: out
  // Probe on pull_resistor_37_node
  Pull_Resistor pull_resistor_37 (.node(pull_resistor_37_node));
  assign pull_resistor_37_node = not_2_out ? program_control_unit_1_iro : 8'bz;  // Controlled_Buffer controlled_buffer_39
  assign controlled_buffer_40_out = not_2_out ? program_control_unit_1_stack_node_enable : 1'bz;  // Controlled_Buffer controlled_buffer_40
  program_counter_driver program_counter_driver_1 (
    .Abi(program_counter_driver_1_abo), .Aboe(pull_resistor_28_node), .Abie(pull_resistor_29_node),
    .Ini(pull_resistor_33_node), .Clk(xor_1_out), .En(1'b1), .Ld(pull_resistor_35_node), .Rst(Rst),
    .Inie(1'b1), .Iso(program_counter_driver_1_iso), .Abo(program_counter_driver_1_abo));
  alu_driver alu_driver_1 (
    .Wo(pull_resistor_13_node), .Oe(pull_resistor_14_node), .Rst(Rst), .Clk(xor_1_out),
    .Op(pull_resistor_19_node), .BW(pull_resistor_17_node), .AW(pull_resistor_16_node),
    .FW(pull_resistor_12_node), .Bi(program_control_unit_1_dbo), .Ai(program_control_unit_1_dbo),
    .Fi(alu_driver_1_fo), .Ie(pull_resistor_15_node), .Ro(program_control_unit_1_dbo), .Fo(alu_driver_1_fo));
  load_store_unit load_store_unit_1 (
    .Rst(Rst), .Isp(pull_resistor_18_node), .Dsp(pull_resistor_23_node), .Dbi(program_control_unit_1_dbo),
    .Roe(pull_resistor_22_node), .Rae(pull_resistor_21_node), .Re(pull_resistor_20_node),
    .We(pull_resistor_27_node), .Clk(xor_1_out), .Foe(pull_resistor_26_node),
    .Abi(program_counter_driver_1_abo), .Sni(controlled_buffer_40_out), .Dbo(program_control_unit_1_dbo),
    .Fo(alu_driver_1_fo), .Abo(program_counter_driver_1_abo));
  addressing_unit addressing_unit_1 (
    .Clk(xor_1_out), .Eah(pull_resistor_25_node), .Eal(pull_resistor_24_node),
    .Dbi(program_control_unit_1_dbo), .Dbie(pull_resistor_31_node), .Rst(Rst), .Aboe(pull_resistor_30_node),
    .Abo(program_counter_driver_1_abo));
  register_file register_file_1 (
    .Rst(Rst), .Dbi(program_control_unit_1_dbo), .Clk(xor_1_out), .Foe(pull_resistor_8_node),
    .Doe(pull_resistor_9_node), .Coe(pull_resistor_10_node), .Boe(pull_resistor_11_node),
    .Aoe(pull_resistor_4_node), .Fie(pull_resistor_5_node), .Die(pull_resistor_6_node),
    .Cie(pull_resistor_7_node), .Bie(pull_resistor_2_node), .Aie(pull_resistor_3_node), .Fi(alu_driver_1_fo),
    .Dbo(program_control_unit_1_dbo), .Fo(alu_driver_1_fo), .Fod(register_file_1_fod));
  // Probe on program_control_unit_1_dbo
  // Probe on program_counter_driver_1_abo
  // Probe on alu_driver_1_fo
  // Probe on program_counter_driver_1_iso
endmodule

module alu (
  input  [7:0] Fi,
  input  [7:0] Ai,
  input  [7:0] Bi,
  input  [6:0] Op,
  output [7:0] Ro,
  output [7:0] Fo
);

  wire adder_1_cout, subtractor_1_bout;
  wire [2:0] bit_extender_1_out, bit_extender_2_out;
  wire [7:0] adder_1_out, and_1_out, not_1_out, or_1_out, shifter_1_out, shifter_2_out, subtractor_1_out;

  Bit_Extender #(.out_width(3), .\type ("zero")) bit_extender_1 (.in(Bi), .out(bit_extender_1_out));
  Bit_Extender #(.out_width(3), .\type ("zero")) bit_extender_2 (.in(Bi), .out(bit_extender_2_out));
  Adder adder_1 (.a(Ai), .b(Bi), .out(adder_1_out), .cin(Fi[0]), .cout(adder_1_cout));
  Subtractor subtractor_1 (.a(Ai), .b(Bi), .out(subtractor_1_out), .bin(Fi[0]), .bout(subtractor_1_bout));
  assign and_1_out = Ai & Bi;  // AND_Gate and_1, 8 bits wide
  assign or_1_out = Ai | Bi;  // OR_Gate or_1, 8 bits wide
  assign not_1_out = ~Bi;  // NOT_Gate not_1, 8 bits wide
  assign Ro = Op[5] ? shifter_1_out : 8'bz;  // Controlled_Buffer controlled_buffer_1
  Shifter #(.shift("rl")) shifter_1 (.in(Ai), .\dist (bit_extender_1_out), .out(shifter_1_out));
  assign Ro = Op[6] ? shifter_2_out : 8'bz;  // Controlled_Buffer controlled_buffer_2
  Shifter #(.shift("rr")) shifter_2 (.in(Ai), .\dist (bit_extender_2_out), .out(shifter_2_out));
  assign Ro = Op[1] ? subtractor_1_out : 8'bz;  // Controlled_Buffer controlled_buffer_3
  assign Ro = Op[2] ? and_1_out : 8'bz;  // Controlled_Buffer controlled_buffer_4
  assign Ro = Op[3] ? or_1_out : 8'bz;  // Controlled_Buffer controlled_buffer_5
  assign Ro = Op[4] ? not_1_out : 8'bz;  // Controlled_Buffer controlled_buffer_6
  assign Ro = Op[0] ? adder_1_out : 8'bz;  // Controlled_Buffer controlled_buffer_7
  assign Fo[0] = Op[0] ? adder_1_cout : 1'bz;  // Controlled_Buffer controlled_buffer_8
  assign Fo[0] = Op[1] ? subtractor_1_bout : 1'bz;  // Controlled_Buffer controlled_buffer_9
  Comparator comparator_1 (.a(Ro), .b({8{1'b0}}), .gt(Fo[2]), .eq(Fo[1]));  // open: lt

  assign Fo[7:3] = {5{1'b0}};
endmodule

module alu_driver (
  input  Wo,
  input  Oe,
  input  Rst,
  input  Clk,
  input  [6:0] Op,
  input  BW,
  input  AW,
  input  FW,
  input  [7:0] Bi,
  input  [7:0] Ai,
  input  [7:0] Fi,
  input  Ie,
  output [7:0] Ro,
  output [7:0] Fo
);

  wire and_1_out;
  wire [6:0] controlled_buffer_4_out;
  wire [7:0] alu_1_fo, alu_1_ro, controlled_buffer_1_out, controlled_buffer_2_out, controlled_buffer_3_out,
       register_1_q, register_2_q, register_3_q, register_4_q, register_5_q;

  and and_1 (and_1_out, Rst, Clk);
  Register register_1 (.D(Fi), .en(FW), .clk(Clk), .Q(register_1_q), .clr(and_1_out));
  Register register_2 (.D(Ai), .en(AW), .clk(Clk), .Q(register_2_q), .clr(and_1_out));
  Register register_3 (.D(Bi), .en(BW), .clk(Clk), .Q(register_3_q), .clr(and_1_out));
  assign controlled_buffer_1_out = Ie ? register_1_q : 8'bz;  // Controlled_Buffer controlled_buffer_1
  assign controlled_buffer_2_out = Ie ? register_2_q : 8'bz;  // Controlled_Buffer controlled_buffer_2
  assign controlled_buffer_3_out = Ie ? register_3_q : 8'bz;  // Controlled_Buffer controlled_buffer_3
  assign controlled_buffer_4_out = Ie ? Op : 7'bz;  // Controlled_Buffer controlled_buffer_4
  Register register_4 (.D(alu_1_ro), .en(Wo), .clk(Clk), .Q(register_4_q));  // open: clr
  alu alu_1 (
    .Fi(controlled_buffer_1_out), .Ai(controlled_buffer_2_out), .Bi(controlled_buffer_3_out),
    .Op(controlled_buffer_4_out), .Ro(alu_1_ro), .Fo(alu_1_fo));
  Register register_5 (.D(alu_1_fo), .en(Wo), .clk(Clk), .Q(register_5_q));  // open: clr
  assign Ro = Oe ? register_4_q : 8'bz;  // Controlled_Buffer controlled_buffer_5
  assign Fo = Oe ? register_5_q : 8'bz;  // Controlled_Buffer controlled_buffer_6
endmodule

module program_counter (
  input  Ini,
  input  Ldi,
  input  Rsti,
  input  Eni,
  input  Clki,
  input  [15:0] Ab,
  output [2:0] Iso,
  output [15:0] About
);

  wire and_1_out, and_2_out, and_3_out, and_4_out, and_5_out, and_6_out, and_7_out, and_8_out, and_9_out,
       counter_1_carry, d_ff_1_q, not_1_out, not_2_out, or_1_out, or_2_out, or_3_out, or_4_out,
       program_counter_decoder_1_cbc, program_counter_decoder_1_ino, program_counter_decoder_1_ldo;
  wire [15:0] multiplexer_1_out;

  Multiplexer #(.width(16)) multiplexer_1 (.in0(16'h8000), .in1(Ab), .out(multiplexer_1_out), .sel(not_1_out));
  not not_1 (not_1_out, Rsti);
  program_counter_decoder program_counter_decoder_1 (
    .Ldi(Ldi), .Ini(Ini), .Ldo(program_counter_decoder_1_ldo), .Ino(program_counter_decoder_1_ino),
    .Cbc(program_counter_decoder_1_cbc));
  and and_1 (and_1_out, Rsti, Clki);
  and and_2 (and_2_out, program_counter_decoder_1_ldo, Clki);
  or or_1 (or_1_out, and_1_out, and_2_out, and_3_out);
  and and_3 (and_3_out, program_counter_decoder_1_ino, Clki);
  and and_4 (and_4_out, Rsti, Clki);
  and and_5 (and_5_out, program_counter_decoder_1_ldo, Clki);
  or or_2 (or_2_out, and_4_out, and_5_out);
  and and_6 (and_6_out, program_counter_decoder_1_ldo, Clki);
  or or_3 (or_3_out, 1'b0, and_6_out, and_7_out, and_8_out, and_9_out);
  and and_7 (and_7_out, program_counter_decoder_1_ino, Clki);
  and and_8 (and_8_out, Rsti, Clki);
  and and_9 (and_9_out, program_counter_decoder_1_cbc, Clki);
  Counter #(.max('h7), .width(3)) counter_1 (
    .clr(or_1_out), .up(1'b1), .count(Eni), .clk(Clki), .carry(counter_1_carry), .Q(Iso));  // open: load, D
  Counter #(.max('hffff), .width(16)) counter_2 (
    .load(or_2_out), .up(1'b1), .count(Eni), .clk(or_4_out), .D(multiplexer_1_out), .Q(About));  // open: clr, carry
  or or_4 (or_4_out, d_ff_1_q, or_3_out);
  D_Flip_Flop d_ff_1 (.D(counter_1_carry), .clk(Clki), .Q(d_ff_1_q), .reset(not_2_out));  // open: Qn, preset
  not not_2 (not_2_out, counter_1_carry);
endmodule

module program_counter_decoder (
  input  Ldi,
  input  Ini,
  output Ldo,
  output Ino,
  output Cbc
);

  wire not_1_out, not_2_out;

  not not_1 (not_1_out, Ini);
  not not_2 (not_2_out, Ldi);
  and and_1 (Ino, Ini, not_2_out);
  and and_2 (Ldo, not_1_out, Ldi);
  and and_3 (Cbc, Ini, Ldi);
endmodule

module program_counter_driver (
  input  [15:0] Abi,
  input  Aboe,
  input  Abie,
  input  Ini,
  input  Clk,
  input  En,
  input  Ld,
  input  Rst,
  input  Inie,
  output [2:0] Iso,
  output [15:0] Abo
);

  wire controlled_buffer_1_out;
  wire [15:0] controlled_buffer_2_out, program_counter_1_about;

  assign controlled_buffer_1_out = Inie ? Ini : 1'bz;  // Controlled_Buffer controlled_buffer_1
  assign controlled_buffer_2_out = Abie ? Abi : 16'bz;  // Controlled_Buffer controlled_buffer_2
  program_counter program_counter_1 (
    .Ini(controlled_buffer_1_out), .Ldi(Ld), .Rsti(Rst), .Eni(En), .Clki(Clk), .Ab(controlled_buffer_2_out),
    .Iso(Iso), .About(program_counter_1_about));
  assign Abo = Aboe ? program_counter_1_about : 16'bz;  // Controlled_Buffer controlled_buffer_3
endmodule

module register_file (
  input  Rst,
  input  [7:0] Dbi,
  input  Clk,
  input  Foe,
  input  Doe,
  input  Coe,
  input  Boe,
  input  Aoe,
  input  Fie,
  input  Die,
  input  Cie,
  input  Bie,
  input  Aie,
  input  [7:0] Fi,
  output [7:0] Dbo,
  output [7:0] Fo,
  output [7:0] Fod
);

  wire and_1_out;
  wire [7:0] A_q, B_q, C_q, D_q;

  and and_1 (and_1_out, Clk, Rst);
  Register A (.D(Dbi), .en(Aie), .clk(Clk), .Q(A_q), .clr(and_1_out));
  Register B (.D(Dbi), .en(Bie), .clk(Clk), .Q(B_q), .clr(and_1_out));
  Register C (.D(Dbi), .en(Cie), .clk(Clk), .Q(C_q), .clr(and_1_out));
  Register D (.D(Dbi), .en(Die), .clk(Clk), .Q(D_q), .clr(and_1_out));
  Register F (.D(Fi), .en(Fie), .clk(Clk), .Q(Fod), .clr(and_1_out));
  assign Dbo = Aoe ? A_q : 8'bz;  // Controlled_Buffer controlled_buffer_1
  assign Dbo = Boe ? B_q : 8'bz;  // Controlled_Buffer controlled_buffer_2
  assign Dbo = Coe ? C_q : 8'bz;  // Controlled_Buffer controlled_buffer_3
  assign Dbo = Doe ? D_q : 8'bz;  // Controlled_Buffer controlled_buffer_4
  assign Fo = Foe ? Fod : 8'bz;  // Controlled_Buffer controlled_buffer_5
endmodule

module load_store_unit (
  input  Rst,
  input  Isp,
  input  Dsp,
  input  [7:0] Dbi,
  input  Roe,
  input  Rae,
  input  Re,
  input  We,
  input  Clk,
  input  Foe,
  input  [15:0] Abi,
  input  Sni,
  output [7:0] Dbo,
  output [7:0] Fo,
  output [15:0] Abo
);

  wire and_1_out, and_3_out, and_4_out, bit_extender_2_out, counter_1_carry, d_ff_1_q, not_1_out,
       stack_select_1_en, stack_select_1_ls;
  wire [7:0] ram_1_dout, rom_1_data;
  wire [14:0] bit_extender_1_out, controlled_buffer_2_out, controlled_buffer_3_out;
  wire [15:0] and_2_out, counter_1_q, shifter_1_out;

  Pull_Resistor pull_resistor_1 (.node(Sni));
  stack_select stack_select_1 (.Dsp(Dsp), .Isp(Isp), .Ls(stack_select_1_ls), .En(stack_select_1_en));
  and and_1 (and_1_out, stack_select_1_en, not_1_out);
  Counter #(.max('h7fff), .width(16)) counter_1 (
    .load(Rst), .up(stack_select_1_ls), .count(and_1_out), .clk(Clk), .D(16'h7fff), .carry(counter_1_carry),
    .Q(counter_1_q));  // open: clr
  assign and_2_out = Abi & 16'h8000;  // AND_Gate and_2, 16 bits wide
  Bit_Extender #(.in_width(16), .out_width(15), .\type ("zero")) bit_extender_1 (.in(Abi), .out(bit_extender_1_out));
  Bit_Extender #(.in_width(16), .out_width(1), .\type ("zero")) bit_extender_2 (
    .in(shifter_1_out), .out(bit_extender_2_out));
  Shifter #(.shift("lr"), .width(16)) shifter_1 (.in(and_2_out), .\dist (4'b1111), .out(shifter_1_out));
  assign Abo = Sni ? counter_1_q : 16'bz;  // Controlled_Buffer controlled_buffer_1
  and and_3 (and_3_out, Re, bit_extender_2_out, Roe);
  assign controlled_buffer_2_out = bit_extender_2_out ? bit_extender_1_out : 15'bz;  // Controlled_Buffer controlled_buffer_2
  not not_1 (not_1_out, bit_extender_2_out);
  ROM #(.addrWidth(15), .misaligned("true")) rom_1 (.addr(controlled_buffer_2_out), .data(rom_1_data));
  assign controlled_buffer_3_out = not_1_out ? bit_extender_1_out : 15'bz;  // Controlled_Buffer controlled_buffer_3
  RAM #(.addrWidth(15), .trigger("high")) ram_1 (
    .addr(controlled_buffer_3_out), .we(We), .oe(and_4_out), .din(Dbi), .dout(ram_1_dout));
  D_Flip_Flop d_ff_1 (.D(counter_1_carry), .clk(Clk), .Q(d_ff_1_q));  // open: Qn, preset, reset
  and and_4 (and_4_out, Re, Rae);
  assign Dbo = and_3_out ? rom_1_data : 8'bz;  // Controlled_Buffer controlled_buffer_4
  assign Dbo = and_4_out ? ram_1_dout : 8'bz;  // Controlled_Buffer controlled_buffer_5
  assign Fo[2] = Foe ? d_ff_1_q : 1'bz;  // Controlled_Buffer controlled_buffer_6

  // Notes on the sheet:
  //   contents of rom_1 (hex, n*v repeats v):
  //   5e 2 60 1 2 6d 0 1
endmodule

module stack_select (
  input  Dsp,
  input  Isp,
  output Ls,
  output En
);

  wire and_2_out, and_3_out, not_1_out, not_2_out;

  not not_1 (not_1_out, Dsp);
  not not_2 (not_2_out, Isp);
  and and_1 (Ls, Dsp, not_2_out);
  and and_2 (and_2_out, not_1_out, Isp);
  or or_1 (En, and_2_out, and_3_out);
  and and_3 (and_3_out, Dsp, not_2_out);
endmodule

module addressing_unit (
  input  Clk,
  input  Eah,
  input  Eal,
  input  [7:0] Dbi,
  input  Dbie,
  input  Rst,
  input  Aboe,
  output [15:0] Abo
);

  wire and_1_out, and_2_out, and_3_out, demultiplexer_2_out0, demultiplexer_2_out1, not_1_out, not_2_out;
  wire [7:0] controlled_buffer_1_out, demultiplexer_1_out0, demultiplexer_1_out1;
  wire [15:0] Lo_q;

  not not_1 (not_1_out, Eal);
  and and_1 (and_1_out, Eah, not_1_out);
  and and_2 (and_2_out, Dbie, not_2_out);
  assign controlled_buffer_1_out = and_2_out ? Dbi : 8'bz;  // Controlled_Buffer controlled_buffer_1
  Demultiplexer #(.disabled("Z"), .tristate("true"), .width(8)) demultiplexer_1 (
    .out0(demultiplexer_1_out0), .out1(demultiplexer_1_out1), .in(controlled_buffer_1_out), .sel(and_1_out));
  Demultiplexer #(.disabled("Z")) demultiplexer_2 (
    .out0(demultiplexer_2_out0), .out1(demultiplexer_2_out1), .in(Clk), .sel(and_1_out));
  not not_2 (not_2_out, Rst);
  Register Lo (
    .D(demultiplexer_1_out0), .en(demultiplexer_2_out0), .clk(demultiplexer_2_out0), .Q(Lo_q[7:0]),
    .clr(and_3_out));
  Pull_Resistor pull_resistor_1 (.node(demultiplexer_1_out0));
  Register Hi (
    .D(demultiplexer_1_out1), .en(demultiplexer_2_out1), .clk(demultiplexer_2_out1), .Q(Lo_q[15:8]),
    .clr(and_3_out));
  Pull_Resistor pull_resistor_2 (.node(demultiplexer_1_out1));
  and and_3 (and_3_out, Rst, Clk);
  assign Abo = Aboe ? Lo_q : 16'bz;  // Controlled_Buffer controlled_buffer_2
endmodule

module program_control_unit (
  input  Rst,
  input  Clk,
  input  [2:0] Isi,
  input  [7:0] Dbi,
  input  [7:0] Fi,
  output RF_A_IN,
  output RF_B_IN,
  output RF_C_IN,
  output RF_D_IN,
  output RF_FLAGS_IN,
  output RF_A_OUT,
  output RF_B_OUT,
  output RF_C_OUT,
  output RF_D_OUT,
  output RF_FLAGS_OUT,
  output ALU_IN,
  output ALU_OUT,
  output ALU_WRITE_OUT,
  output ALU_WRITE_F,
  output ALU_WRITE_B,
  output ALU_WRITE_A,
  output [6:0] ALU_OP,
  output LSU_INCREMENT_STACK_POINTER,
  output LSU_DECREMENT_STACK_POINTER,
  output LSU_ROM_ENABLE,
  output LSU_RAM_ENABLE,
  output LSU_READ_ENABLE,
  output LSU_WRITE_ENABLE,
  output LSU_FLAGS_OUT,
  output EAU_HI_SELECT,
  output EAU_LOW_SELECT,
  output EAU_DATA_BUS_IN,
  output EAU_ADDRESS_BUS_IN,
  output PC_ADDRESS_BUS_IN,
  output PC_ADDRESS_BUS_OUT,
  output PC_SKIP_TO_NEXT_INSTRUCTION,
  output PC_ENABLE_UNUSED,
  output PC_LOAD_VALUE,
  output CONNECT_F_TO_DATA_BUS,
  output RF_TEMP_IN,
  output RF_TEMP_OUT,
  output JUMP_ENABLE,
  output [7:0] Dbo,
  output [7:0] Iro,
  output STACK_NODE_ENABLE
);

  wire and_1_out, and_2_out, comparator_1_eq, not_1_out, not_2_out;
  wire [2:0] register_1_q;
  wire [7:0] bit_extender_1_out, controlled_buffer_1_out, multiplexer_1_out, rom_1_data_2;
  wire [10:0] adder_1_out, bit_extender_2_out;
  wire [31:0] rom_1_data;

  Register #(.width(3)) register_1 (.D(Isi), .en(Clk), .clk(Clk), .Q(register_1_q), .clr(not_1_out));
  not not_1 (not_1_out, Clk);
  and and_1 (and_1_out, Clk, Rst);
  not not_2 (not_2_out, Rst);
  assign controlled_buffer_1_out = rom_1_data[26] ? Dbi : 8'bz;  // Controlled_Buffer controlled_buffer_1
  Multiplexer #(.width(8)) multiplexer_1 (
    .in0({8{1'b0}}), .in1(controlled_buffer_1_out), .out(multiplexer_1_out), .sel(not_2_out));
  Comparator #(.mode("unsigned"), .width(3)) comparator_1 (
    .a(register_1_q), .b(3'b000), .eq(comparator_1_eq));  // open: gt, lt
  and and_2 (and_2_out, comparator_1_eq, Clk);
  Register IR (.D(multiplexer_1_out), .en(and_2_out), .clk(and_2_out), .Q(Iro), .clr(and_1_out));
  Bit_Extender #(.out_width(8), .\type ("zero")) bit_extender_1 (.in(Iro), .out(bit_extender_1_out));
  assign bit_extender_2_out = {{8{1'b0}}, Isi};  // Bit_Extender bit_extender_2
  Adder #(.width(11)) adder_1 (
    .a({bit_extender_1_out, 3'b000}), .b(bit_extender_2_out), .out(adder_1_out));  // open: cin, cout
  ROM #(.addrWidth(11), .dataWidth(64)) rom_1 (
    .addr(adder_1_out),
    .data({ALU_WRITE_A, ALU_WRITE_B, ALU_WRITE_F, ALU_WRITE_OUT, ALU_OUT, ALU_IN, RF_FLAGS_OUT, RF_D_OUT, RF_C_OUT, RF_B_OUT, RF_A_OUT, RF_FLAGS_IN, RF_D_IN, RF_C_IN, RF_B_IN, RF_A_IN, EAU_LOW_SELECT, EAU_HI_SELECT, LSU_FLAGS_OUT, LSU_WRITE_ENABLE, LSU_READ_ENABLE, LSU_RAM_ENABLE, LSU_ROM_ENABLE, LSU_DECREMENT_STACK_POINTER, LSU_INCREMENT_STACK_POINTER, ALU_OP, rom_1_data[31:26], RF_TEMP_OUT, RF_TEMP_IN, CONNECT_F_TO_DATA_BUS, PC_LOAD_VALUE, PC_ENABLE_UNUSED, PC_SKIP_TO_NEXT_INSTRUCTION, PC_ADDRESS_BUS_OUT, PC_ADDRESS_BUS_IN, EAU_ADDRESS_BUS_IN, EAU_DATA_BUS_IN, rom_1_data_2[0], rom_1_data_2[1], rom_1_data_2[2], rom_1_data_2[3], rom_1_data_2[4], rom_1_data_2[5], rom_1_data_2[6], rom_1_data_2[7], rom_1_data[7], STACK_NODE_ENABLE, rom_1_data[5:0]}));
  assign Dbo = rom_1_data[7] ? rom_1_data_2 : 8'bz;  // Controlled_Buffer controlled_buffer_2
  jump_unit jump_unit_1 (.JEZ(rom_1_data[27]), .JCS(rom_1_data[28]), .JGZ(rom_1_data[29]), .Fi(Fi), .JE(JUMP_ENABLE));

  // Notes on the sheet:
  //   contents of rom_1 (hex, n*v repeats v):
  //   a0004080000 100000 6*0 a0004080000 10000000800880 100000 5*0 a0004080000 8420000000000000
  //   4440000000000000 2600000000000000 1400000100000000 811000000000000 100000 0 a0004080000
  //   8420000000000000 4480000000000000 2600000000000000 1400000100000000 811000000000000 100000 0
  //   a0004080000 8420000000000000 4500000000000000 2600000000000000 1400000100000000 811000000000000
  //   100000 0 a0004080000 8420000000000000 500000 8a0000590000 4a0000090000 44000c0000020000
  //   1400000100000000 811000000000000 8*0 a0004080000 8440000000000000 4420000000000000 2600000000000000
  //   1400000100000000 812000000000000 100000 0 a0004080000 8440000000000000 4480000000000000
  //   2600000000000000 1400000100000000 812000000000000 100000 0 a0004080000 8440000000000000
  //   4500000000000000 2600000000000000 1400000100000000 812000000000000 100000 0 a0004080000
  //   8440000000000000 500000 8a0000590000 4a0000090000 44000c0000020000 1400000100000000 812000000000000
  //   8*0 a0004080000 8480000000000000 4420000000000000 2600000000000000 1400000100000000 814000000000000
  //   100000 0 a0004080000 8480000000000000 4440000000000000 2600000000000000 1400000100000000
  //   814000000000000 100000 0 a0004080000 8480000000000000 4500000000000000 2600000000000000
  //   1400000100000000 814000000000000 100000 0 a0004080000 8480000000000000 500000 8a0000590000
  //   4a0000090000 44000c0000020000 1400000100000000 814000000000000 8*0 a0004080000 8500000000000000
  //   4420000000000000 2600000000000000 1400000100000000 818000000000000 100000 0 a0004080000
  //   8500000000000000 4440000000000000 2600000000000000 1400000100000000 818000000000000 100000 0
  //   a0004080000 8500000000000000 4480000000000000 2600000000000000 1400000100000000 818000000000000
  //   100000 0 a0004080000 8500000000000000 500000 8a0000590000 4a0000090000 44000c0000020000
  //   1400000100000000 818000000000000 8*0 a0004080000 8420000000000000 4440000000000000 2600000000000000
  //   1400000200000000 811000000000000 100000 0 a0004080000 8420000000000000 4480000000000000
  //   2600000000000000 1400000200000000 811000000000000 100000 0 a0004080000 8420000000000000
  //   4500000000000000 2600000000000000 1400000200000000 811000000000000 100000 0 a0004080000
  //   8420000000000000 500000 8a0000590000 4a0000090000 44000c0000020000 1400000200000000 811000000000000
  //   8*0 a0004080000 8440000000000000 4420000000000000 2600000000000000 1400000200000000 812000000000000
  //   100000 0 a0004080000 8440000000000000 4480000000000000 2600000000000000 1400000200000000
  //   812000000000000 100000 0 a0004080000 8440000000000000 4500000000000000 2600000000000000
  //   1400000200000000 812000000000000 100000 0 a0004080000 8440000000000000 500000 8a0000590000
  //   4a0000090000 44000c0000020000 1400000200000000 812000000000000 8*0 a0004080000 8480000000000000
  //   4420000000000000 2600000000000000 1400000200000000 814000000000000 100000 0 a0004080000
  //   8480000000000000 4440000000000000 2600000000000000 1400000200000000 814000000000000 100000 0
  //   a0004080000 8480000000000000 4500000000000000 2600000000000000 1400000200000000 814000000000000
  //   100000 0 a0004080000 8480000000000000 500000 8a0000590000 4a0000090000 44000c0000020000
  //   1400000200000000 814000000000000 8*0 a0004080000 8500000000000000 4420000000000000 2600000000000000
  //   1400000200000000 818000000000000 100000 0 a0004080000 8500000000000000 4440000000000000
  //   2600000000000000 1400000200000000 818000000000000 100000 0 a0004080000 8500000000000000
  //   4480000000000000 2600000000000000 1400000200000000 818000000000000 100000 0 a0004080000
  //   8500000000000000 500000 8a0000590000 4a0000090000 44000c0000020000 1400000200000000 818000000000000
  //   8*0 a0004080000 8420000000000000 4440000000000000 2600000000000000 1400000400000000 811000000000000
  //   100000 0 a0004080000 8420000000000000 4480000000000000 2600000000000000 1400000400000000
  //   811000000000000 100000 0 a0004080000 8420000000000000 4500000000000000 2600000000000000
  //   1400000400000000 811000000000000 100000 0 a0004080000 8420000000000000 500000 8a0000590000
  //   4a0000090000 44000c0000020000 1400000400000000 811000000000000 8*0 a0004080000 8440000000000000
  //   4420000000000000 26000000000000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
endmodule

module jump_unit (
  input  JEZ,
  input  JCS,
  input  JGZ,
  input  [7:0] Fi,
  output JE
);

  wire and_1_out, and_2_out, and_3_out;

  and and_1 (and_1_out, Fi[0], JCS);
  and and_2 (and_2_out, Fi[1], JEZ);
  and and_3 (and_3_out, Fi[2], JGZ);
  or or_1 (JE, and_1_out, and_2_out, and_3_out);
endmodule
